# Fritzing sketch Cumulative-Project-Schematics (saved by Fritzing 0.9.3b)
breadboards: 1

parts:
  Part1 = Arduino Uno (Rev3)
  LED1 = LED - 5mm [color="Green (555nm)" package="5 mm [THT]"]
  LED2 = LED - 5mm [color="Green (555nm)" package="5 mm [THT]"]
  LED3 = LED - 5mm [color="Red (633nm)" package="5 mm [THT]"]
  LED4 = LED - 5mm [color="Red (633nm)" package="5 mm [THT]"]
  R1 = Resistor [tolerance=±5% resistance=220 package=THT]
  R2 = Resistor [tolerance=±5% resistance=220 package=THT]
  R3 = Resistor [tolerance=±5% resistance=220 package=THT]
  R4 = Resistor [tolerance=±5% resistance=220 package=THT]
  Part2 = Soil Moisture Sensor
  R5 = Resistor [tolerance=±5% resistance=10k package=THT]
  R6 = Photocell (LDR) [package=THT]

nets:
  N1: Part1.A0, Part2.SIG
  N2: Part1.A1, R5.Pin_1, R6.pin_0
  GND: Part1.GND, R1.Pin_0, R2.Pin_0, R3.Pin_0, R4.Pin_0, Part2.GND, R5.Pin_0
  N3: Part1.D2, LED4.cathode
  N4: Part1.D3_PWM, LED2.cathode
  N5: Part1.D4, LED3.cathode
  N6: Part1.D5_PWM, LED1.cathode
  5V: Part1.5V, Part2.VCC, R6.pin_1
  N7: LED1.anode, R1.Pin_1
  N8: LED2.anode, R3.Pin_1
  N9: LED3.anode, R2.Pin_1
  N10: LED4.anode, R4.Pin_1
